// Logisim project Simple16Console.circ as structural Verilog: 19 circuits, main circuit main
module main (
);

  wire and_1_out, clock_1_out, comparator_1_eq, cpu_1_asciienable, cpu_1_jump, cpu_1_outenable,
       cpu_1_termclear, keyboard_1_avail, megaor_1_out_2, not_1_out, not_2_out, not_3_out, not_4_out,
       or_1_out, OutEnable_q, overide_q, register_1_q, reset_out, resetScreen_q;
  wire [4:0] bit_extender_1_out, counter_1_q;
  wire [6:0] bit_extender_2_out, bit_extender_4_out, bit_extender_5_out, bit_extender_6_out, keyboard_1_data,
       ram_1_dout;
  wire [7:0] programRom_data, programRom_data_2;
  wire [11:0] LT_out;
  wire [15:0] bit_extender_3_out, bit_extender_7_out, cpu_1_ascii, cpu_1_position, easycounter_1_value,
       joystick_1_x, position_q;
  wire [23:0] cpu_1_color;
  wire [63:16] programRom_data_3;

  Clock clock_1 (.out(clock_1_out));
  Register #(.width(1)) overide (.D(cpu_1_jump), .en(not_1_out), .clk(not_2_out), .Q(overide_q));  // open: clr
  not not_1 (not_1_out, clock_1_out);
  not not_2 (not_2_out, clock_1_out);
  easyCounter easycounter_1 (
    .update(clock_1_out), .overideVal(programRom_data_3[63:48]), .overide(overide_q),
    .value(easycounter_1_value));
  ROM #(.addrWidth(16), .dataWidth(64)) programRom (
    .addr(easycounter_1_value), .data({programRom_data_3, programRom_data_2, programRom_data}));
  Bit_Extender #(.in_width(16), .out_width(5), .\type ("zero")) bit_extender_1 (
    .in(programRom_data_3[63:48]), .out(bit_extender_1_out));
  Bit_Extender #(.out_width(7), .\type ("zero")) bit_extender_2 (.in(programRom_data), .out(bit_extender_2_out));
  assign bit_extender_3_out = {{4{1'b0}}, LT_out};  // Bit_Extender bit_extender_3
  CPU cpu_1 (
    .clock(clock_1_out), .destination(bit_extender_1_out), .in1(programRom_data_3[31:16]),
    .opcode(bit_extender_2_out), .in2(programRom_data_3[47:32]), .sticks(joystick_1_x),
    .buttons(bit_extender_3_out), .asciiIn(bit_extender_7_out), .constants(programRom_data_2),
    .Position(cpu_1_position), .outEnable(cpu_1_outenable), .Color(cpu_1_color), .jump(cpu_1_jump),
    .asciiEnable(cpu_1_asciienable), .ascii(cpu_1_ascii), .termClear(cpu_1_termclear));
  Register #(.trigger("high"), .width(1)) OutEnable (
    .D(cpu_1_outenable), .en(1'b1), .clk(clock_1_out), .Q(OutEnable_q));  // open: clr
  Bit_Extender #(.in_width(16), .out_width(7), .\type ("input")) bit_extender_4 (
    .in(cpu_1_ascii), .out(bit_extender_4_out));  // open: extend
  Register #(.trigger("high"), .width(16)) position (
    .D(cpu_1_position), .en(1'b1), .clk(clock_1_out), .Q(position_q));  // open: clr
  Register #(.width(1)) resetScreen (.D(clock_1_out), .en(1'b1), .clk(clock_1_out), .Q(resetScreen_q));  // open: clr
  megaOR megaor_1 (.in_1(position_q), .out_2(megaor_1_out_2));
  Button reset (.out(reset_out));
  // Digital_Oscilloscope #(.frontlines("both")) digital_oscilloscope_1: pin names not known; wires that end beside it: clock_1_out, OutEnable_q, megaor_1_out_2
  or or_1 (or_1_out, reset_out, ~resetScreen_q);  // OR_Gate
  Bit_Extender #(.out_width(7), .\type ("zero")) bit_extender_5 (.in(position_q[7:0]), .out(bit_extender_5_out));
  Bit_Extender #(.out_width(7), .\type ("zero")) bit_extender_6 (.in(position_q[15:8]), .out(bit_extender_6_out));
  Button LT (.out(LT_out[0]));
  Button LB (.out(LT_out[2]));
  Joystick #(.bits(5)) joystick_1 (.x(joystick_1_x[4:0]), .y(joystick_1_x[9:5]));
  Button u (.out(LT_out[8]));
  Button l (.out(LT_out[9]));
  Button r (.out(LT_out[10]));
  Button d (.out(LT_out[11]));
  Button Y (.out(LT_out[7]));
  Button X (.out(LT_out[6]));
  Button A (.out(LT_out[4]));
  // RGB_Video #(.cursor("No Cursor")) rgb_video_1: pin names not known; wires that end beside it: or_1_out, clock_1_out, OutEnable_q, bit_extender_5_out, bit_extender_6_out, cpu_1_color
  Button RT (.out(LT_out[1]));
  Button RB (.out(LT_out[3]));
  Button B (.out(LT_out[5]));
  Joystick #(.bits(3)) joystick_2 (.x(joystick_1_x[12:10]), .y(joystick_1_x[15:13]));
  and and_1 (and_1_out, cpu_1_asciienable, clock_1_out);
  TTY tty_1 (.data(bit_extender_4_out), .clk(and_1_out), .clr(cpu_1_termclear));  // open: we
  Comparator #(.mode("unsigned"), .width(7)) comparator_1 (
    .a(keyboard_1_data), .b(7'b0001000), .eq(comparator_1_eq));  // open: gt, lt
  Register #(.trigger("high"), .width(1)) register_1 (.Q(register_1_q));  // open: D, en, clk, clr
  TTY #(.rows(1)) tty_2 (.data(keyboard_1_data), .clk(keyboard_1_avail));  // open: we, clr
  Counter #(.max('h1f), .width(5)) counter_1 (
    .up(not_3_out), .count(keyboard_1_avail), .clk(clock_1_out), .Q(counter_1_q));  // open: clr, load, D, carry
  not not_3 (not_3_out, comparator_1_eq);
  Keyboard keyboard_1 (
    .clk(clock_1_out), .re(not_4_out), .avail(keyboard_1_avail), .data(keyboard_1_data));  // open: clr
  not not_4 (not_4_out, register_1_q);
  RAM #(.addrWidth(5), .clearpin("true"), .dataWidth(7)) ram_1 (
    .addr(counter_1_q), .we(keyboard_1_avail), .oe(clock_1_out), .clk(clock_1_out), .din(keyboard_1_data),
    .dout(ram_1_dout));  // open: clr
  assign bit_extender_7_out = {{9{1'b0}}, ram_1_dout};  // Bit_Extender bit_extender_7

  // Notes on the sheet:
  //   contents of programRom (hex, n*v repeats v):
  //   707 11110369 1000000000269 100008001e060a 13000b001e060a 1c000000000369 1d000000000369
  //   1e000000010269 1c0000ffff0369 1d0000ffff0369 1e000000000269 2000000000707 2000800020207 ff0000000233
  //   200000010 5000000000707 2000000000270 2000000020220 c000000000707 2000000000270 200000002021f
  //   c000000000707
endmodule

module easyCounter (
  input  update,
  input  [15:0] overideVal,
  input  overide,
  output [15:0] value
);

  wire [15:0] adder_1_out, multiplexer_1_out;

  Register #(.width(16)) PC (.D(multiplexer_1_out), .en(1'b1), .clk(update), .Q(value));  // open: clr
  Adder #(.width(16)) adder_1 (.a(value), .b(16'h1), .out(adder_1_out));  // open: cin, cout
  Multiplexer #(.width(16)) multiplexer_1 (.in0(adder_1_out), .in1(overideVal), .out(multiplexer_1_out), .sel(overide));
endmodule

module registers (
  input  [15:0] data,
  input  [4:0] selectOut1,
  input  save,
  input  [4:0] selectSave,
  input  [15:0] buttons,
  input  [15:0] sticks,
  input  [4:0] selectOut2,
  output [15:0] Out1,
  output [15:0] Out2,
  output [15:0] finalOutput,
  output finalOutputSwitch,
  output [23:0] ColorOut
);

  wire decoder_1_out0, decoder_1_out1, decoder_1_out2, decoder_1_out3, decoder_1_out4, decoder_1_out5,
       decoder_1_out6, decoder_1_out7, decoder_1_out8, decoder_1_out9, decoder_1_out10, decoder_1_out11,
       decoder_1_out12, decoder_1_out13, decoder_1_out14, decoder_1_out15, decoder_1_out16, decoder_1_out17,
       decoder_1_out18, decoder_1_out19, decoder_1_out20, decoder_1_out21, decoder_1_out22, decoder_1_out23,
       decoder_1_out24, decoder_1_out25, decoder_1_out26, decoder_1_out27, decoder_1_out28, decoder_1_out29;
  wire [15:0] bit_extender_1_out, reg1_v, reg2_v, reg3_v, reg4_v, reg5_v, reg6_v, reg7_v, reg8_v, reg9_v,
       reg10_v, reg11_v, reg12_v, reg13_v, reg14_v, reg15_v, reg16_v, reg17_v, reg18_v, reg19_v, reg20_v,
       reg21_v, reg22_v, reg23_v, reg24_v, reg25_v, reg26_v, reg27_v, reg28_v;
  wire [15:8] reg30_v;

  Decoder #(.select(5)) decoder_1 (
    .out0(decoder_1_out0), .out1(decoder_1_out1), .out2(decoder_1_out2), .out3(decoder_1_out3),
    .out4(decoder_1_out4), .out5(decoder_1_out5), .out6(decoder_1_out6), .out7(decoder_1_out7),
    .out8(decoder_1_out8), .out9(decoder_1_out9), .out10(decoder_1_out10), .out11(decoder_1_out11),
    .out12(decoder_1_out12), .out13(decoder_1_out13), .out14(decoder_1_out14), .out15(decoder_1_out15),
    .out16(decoder_1_out16), .out17(decoder_1_out17), .out18(decoder_1_out18), .out19(decoder_1_out19),
    .out20(decoder_1_out20), .out21(decoder_1_out21), .out22(decoder_1_out22), .out23(decoder_1_out23),
    .out24(decoder_1_out24), .out25(decoder_1_out25), .out26(decoder_1_out26), .out27(decoder_1_out27),
    .out28(decoder_1_out28), .out29(decoder_1_out29), .out30(finalOutputSwitch), .sel(selectSave), .en(save));  // open: out31
  assign finalOutput = data & bit_extender_1_out;  // AND_Gate and_1, 16 bits wide
  assign bit_extender_1_out = {{15{finalOutputSwitch}}, finalOutputSwitch};  // Bit_Extender bit_extender_1
  alwaysOutReg reg1 (.D(data), .W(decoder_1_out0), .V(reg1_v));
  alwaysOutReg reg2 (.D(data), .W(decoder_1_out1), .V(reg2_v));
  alwaysOutReg reg3 (.D(data), .W(decoder_1_out2), .V(reg3_v));
  alwaysOutReg reg4 (.D(data), .W(decoder_1_out3), .V(reg4_v));
  alwaysOutReg reg5 (.D(data), .W(decoder_1_out4), .V(reg5_v));
  alwaysOutReg reg6 (.D(data), .W(decoder_1_out5), .V(reg6_v));
  alwaysOutReg reg7 (.D(data), .W(decoder_1_out6), .V(reg7_v));
  alwaysOutReg reg8 (.D(data), .W(decoder_1_out7), .V(reg8_v));
  alwaysOutReg reg9 (.D(data), .W(decoder_1_out8), .V(reg9_v));
  alwaysOutReg reg10 (.D(data), .W(decoder_1_out9), .V(reg10_v));
  alwaysOutReg reg11 (.D(data), .W(decoder_1_out10), .V(reg11_v));
  alwaysOutReg reg12 (.D(data), .W(decoder_1_out11), .V(reg12_v));
  alwaysOutReg reg13 (.D(data), .W(decoder_1_out12), .V(reg13_v));
  alwaysOutReg reg14 (.D(data), .W(decoder_1_out13), .V(reg14_v));
  alwaysOutReg reg15 (.D(data), .W(decoder_1_out14), .V(reg15_v));
  alwaysOutReg reg16 (.D(data), .W(decoder_1_out15), .V(reg16_v));
  alwaysOutReg reg17 (.D(data), .W(decoder_1_out16), .V(reg17_v));
  alwaysOutReg reg18 (.D(data), .W(decoder_1_out17), .V(reg18_v));
  alwaysOutReg reg19 (.D(data), .W(decoder_1_out18), .V(reg19_v));
  alwaysOutReg reg20 (.D(data), .W(decoder_1_out19), .V(reg20_v));
  alwaysOutReg reg21 (.D(data), .W(decoder_1_out20), .V(reg21_v));
  alwaysOutReg reg22 (.D(data), .W(decoder_1_out21), .V(reg22_v));
  alwaysOutReg reg23 (.D(data), .W(decoder_1_out22), .V(reg23_v));
  alwaysOutReg reg24 (.D(data), .W(decoder_1_out23), .V(reg24_v));
  alwaysOutReg reg25 (.D(data), .W(decoder_1_out24), .V(reg25_v));
  alwaysOutReg reg26 (.D(data), .W(decoder_1_out25), .V(reg26_v));
  alwaysOutReg reg27 (.D(data), .W(decoder_1_out26), .V(reg27_v));
  alwaysOutReg reg28 (.D(data), .W(decoder_1_out27), .V(reg28_v));
  alwaysOutReg reg29 (.D(data), .W(decoder_1_out28), .V(ColorOut[15:0]));
  alwaysOutReg reg30 (.D(data), .W(decoder_1_out29), .V({reg30_v, ColorOut[23:16]}));
  LedBar extraBits (
    .led0(reg30_v[8]), .led1(reg30_v[9]), .led2(reg30_v[10]), .led3(reg30_v[11]), .led4(reg30_v[12]),
    .led5(reg30_v[13]), .led6(reg30_v[14]), .led7(reg30_v[15]));
  DualMultiplexer dualMul (
    .in1(reg1_v), .in2(reg2_v), .in3(reg3_v), .in4(reg4_v), .in5(reg5_v), .in6(reg6_v), .in7(reg7_v),
    .in8(reg8_v), .in9(reg9_v), .in10(reg10_v), .s1(selectOut1), .in11(reg11_v), .in12(reg12_v),
    .in13(reg13_v), .in14(reg14_v), .in15(reg15_v), .in16(reg16_v), .in17(reg17_v), .in18(reg18_v),
    .in19(reg19_v), .in20(reg20_v), .in21(reg21_v), .in22(reg22_v), .in23(reg23_v), .in24(reg24_v),
    .in25(reg25_v), .in26(reg26_v), .in27(reg27_v), .in28(reg28_v), .in29(ColorOut[15:0]), .s2(selectOut2),
    .in30({reg30_v, ColorOut[23:16]}), .in31(buttons), .in32(sticks), .out1(Out1), .out2(Out2));
endmodule

module alwaysOutReg (
  input  [15:0] D,
  input  W,
  output [15:0] V
);

  Register #(.trigger("falling"), .width(16)) register_1 (.D(D), .en(1'b1), .clk(W), .Q(V));  // open: clr
endmodule

module DualMultiplexer (
  input  [15:0] in1,
  input  [15:0] in2,
  input  [15:0] in3,
  input  [15:0] in4,
  input  [15:0] in5,
  input  [15:0] in6,
  input  [15:0] in7,
  input  [15:0] in8,
  input  [15:0] in9,
  input  [15:0] in10,
  input  [4:0] s1,
  input  [15:0] in11,
  input  [15:0] in12,
  input  [15:0] in13,
  input  [15:0] in14,
  input  [15:0] in15,
  input  [15:0] in16,
  input  [15:0] in17,
  input  [15:0] in18,
  input  [15:0] in19,
  input  [15:0] in20,
  input  [15:0] in21,
  input  [15:0] in22,
  input  [15:0] in23,
  input  [15:0] in24,
  input  [15:0] in25,
  input  [15:0] in26,
  input  [15:0] in27,
  input  [15:0] in28,
  input  [15:0] in29,
  input  [4:0] s2,
  input  [15:0] in30,
  input  [15:0] in31,
  input  [15:0] in32,
  output [15:0] out1,
  output [15:0] out2
);

  Multiplexer #(.select(5), .width(16)) multiplexer_1 (
    .in0(in1), .in1(in2), .in2(in3), .in3(in4), .in4(in5), .in5(in6), .in6(in7), .in7(in8), .in8(in9),
    .in9(in10), .in10(in11), .in11(in12), .in12(in13), .in13(in14), .in14(in15), .in15(in16), .in16(in17),
    .in17(in18), .in18(in19), .in19(in20), .in20(in21), .in21(in22), .in22(in23), .in23(in24), .in24(in25),
    .in25(in26), .in26(in27), .in27(in28), .in28(in29), .in29(in30), .in30(in31), .in31(in32), .out(out1),
    .sel(s1));
  Multiplexer #(.select(5), .width(16)) multiplexer_2 (
    .in0(in1), .in1(in2), .in2(in3), .in3(in4), .in4(in5), .in5(in6), .in6(in7), .in7(in8), .in8(in9),
    .in9(in10), .in10(in11), .in11(in12), .in12(in13), .in13(in14), .in14(in15), .in15(in16), .in16(in17),
    .in17(in18), .in18(in19), .in19(in20), .in20(in21), .in21(in22), .in22(in23), .in23(in24), .in24(in25),
    .in25(in26), .in26(in27), .in27(in28), .in28(in29), .in29(in30), .in30(in31), .in31(in32), .out(out2),
    .sel(s2));
endmodule

module CPU (
  input  clock,
  input  [4:0] destination,
  input  [15:0] in1,
  input  [6:0] opcode,
  input  [15:0] in2,
  input  [15:0] sticks,
  input  [15:0] buttons,
  input  [15:0] asciiIn,
  input  [7:0] constants,
  output [15:0] Position,
  output outEnable,
  output [23:0] Color,
  output jump,
  output asciiEnable,
  output [15:0] ascii,
  output termClear
);

  wire and_1_out, and_2_out;
  wire [4:0] bit_extender_1_out, bit_extender_2_out;
  wire [7:0] not_1_out;
  wire [15:0] alu_1_value, aluinputadapter_1_out1, aluinputadapter_1_out2, blu_1_ramout, registers_1_out1,
       registers_1_out2;

  Bit_Extender #(.in_width(16), .out_width(5), .\type ("zero")) bit_extender_1 (.in(in1), .out(bit_extender_1_out));
  Bit_Extender #(.in_width(16), .out_width(5), .\type ("zero")) bit_extender_2 (.in(in2), .out(bit_extender_2_out));
  and and_1 (and_1_out, clock, not_1_out[2]);
  registers registers_1 (
    .data(alu_1_value), .selectOut1(bit_extender_1_out), .save(and_1_out), .selectSave(destination),
    .buttons(buttons), .sticks(sticks), .selectOut2(bit_extender_2_out), .Out1(registers_1_out1),
    .Out2(registers_1_out2), .finalOutput(Position), .finalOutputSwitch(outEnable), .ColorOut(Color));
  assign not_1_out = ~constants;  // NOT_Gate not_1, 8 bits wide
  ALUInputAdapter aluinputadapter_1 (
    .in1(in1), .in2(in2), .regIn1(registers_1_out1), .regIn2(registers_1_out2), .ConstByte(not_1_out),
    .out1(aluinputadapter_1_out1), .out2(aluinputadapter_1_out2));
  and and_2 (and_2_out, constants[2], clock);
  ALU alu_1 (
    .in2(aluinputadapter_1_out2), .in1(aluinputadapter_1_out1), .RAMIn(blu_1_ramout), .clock(clock),
    .opcode(opcode), .clockCTR(clock), .value(alu_1_value));  // open: ascii
  BLU blu_1 (
    .in1(aluinputadapter_1_out1), .in2(aluinputadapter_1_out2), .update(and_2_out), .opcode(opcode[3:0]),
    .clock(clock), .jump(jump), .RAMOut(blu_1_ramout), .asciiEnable(asciiEnable), .asciiOut(ascii),
    .clear(termClear));
endmodule

module ALU (
  input  [15:0] in2,
  input  [15:0] in1,
  input  [15:0] RAMIn,
  input  clock,
  input  [6:0] opcode,
  input  clockCTR,
  input  [15:0] ascii,
  output [15:0] value
);

  wire adder_13_cout, adder_15_cout, bitchecker_1_bit, comparator_1_eq, comparator_1_gt, comparator_1_lt,
       comparator_2_gt, comparator_2_lt, comparator_3_eq, comparator_3_gt, comparator_3_lt, comparator_4_gt,
       comparator_4_lt, comparator_5_gt, comparator_5_lt, comparator_6_gt, comparator_6_lt, dipswitch_1_p1,
       fpcomparator_1_p3, fpcomparator_1_p4, fpcomparator_1_p5, fpcomparator_2_p3, fpcomparator_2_p4,
       fpcomparator_2_p5, fpcomparator_3_p3, fpcomparator_3_p4, fpcomparator_4_p1, priority_encoder_1_gs,
       subtractor_9_bout;
  wire [1:0] bit_extender_5_out;
  wire [3:0] adder_2_out, adder_3_out, adder_4_out, adder_5_out, adder_6_out, adder_7_out, and_11_out,
       binary_to_bcd_converter_1_p2, binary_to_bcd_converter_1_p3, binary_to_bcd_converter_1_p4,
       bit_extender_2_out, bit_extender_6_out, bitfinder_1_index, bitfinder_2_index, bitfinder_3_index,
       bitfinder_4_index, divider_3_out, divider_4_out, divider_5_out, divider_6_out, divider_7_out,
       divider_8_out, inttofp_4_p2, multiplexer_1_out, multiplier_7_out, multiplier_8_out, multiplier_9_out,
       multiplier_10_out, multiplier_11_out, multiplier_12_out, nibbleify_1_out_3, nibbleify_1_out_4,
       nibbleify_1_out_5, nibbleify_1_out_6, nibbleify_1_out_7, nibbleify_1_out_8, nibbleify_1_out_9,
       nibbleify_1_out_10, nibbleify_2_out_3, nibbleify_2_out_4, nibbleify_2_out_5, nibbleify_2_out_6,
       nibbleify_2_out_7, nibbleify_2_out_8, nibbleify_2_out_9, nibbleify_2_out_10, nibbleify_3_out_3,
       nibbleify_3_out_4, nibbleify_3_out_5, nibbleify_3_out_6, nibbleify_3_out_7, nibbleify_3_out_8,
       nibbleify_3_out_9, nibbleify_3_out_10, nibbleify_4_out_3, nibbleify_4_out_4, nibbleify_4_out_5,
       nibbleify_4_out_6, nibbleify_4_out_7, nibbleify_4_out_8, nibbleify_4_out_9, nibbleify_4_out_10,
       nibblifysingleinput_1_out_2, nibblifysingleinput_1_out_3, nibblifysingleinput_1_out_4,
       nibblifysingleinput_1_out_5, nibblifysingleinput_2_out_2, nibblifysingleinput_2_out_3,
       nibblifysingleinput_2_out_4, nibblifysingleinput_2_out_5, nibblifysingleinput_3_out_2,
       nibblifysingleinput_3_out_3, nibblifysingleinput_3_out_4, nibblifysingleinput_3_out_5,
       nibblifysingleinput_4_out_2, nibblifysingleinput_4_out_3, nibblifysingleinput_4_out_4,
       nibblifysingleinput_4_out_5, nibblifysingleinput_5_out_2, nibblifysingleinput_5_out_3,
       nibblifysingleinput_5_out_4, nibblifysingleinput_5_out_5, priority_encoder_1_out, subtractor_1_out,
       subtractor_2_out, subtractor_3_out, subtractor_4_out, subtractor_5_out, subtractor_6_out;
  wire [4:0] bitadder_1_out;
  wire [5:0] bitadder_2_out;
  wire [6:0] adder_13_out, adder_14_out, bit_extender_3_out, bit_extender_4_out;
  wire [7:0] bit_extender_27_out, bit_extender_28_out;
  wire [12:0] bit_extender_1_out;
  wire [15:0] adder_1_out, adder_8_out, adder_9_out, adder_10_out, adder_11_out, adder_12_out, adder_15_out,
       adder_16_out, adder_17_out, and_1_out, and_2_out, and_3_out, and_4_out, and_5_out, and_6_out,
       and_7_out, and_8_out, and_9_out, and_10_out, and_12_out, bit_extender_7_out, bit_extender_8_out,
       bit_extender_9_out, bit_extender_10_out, bit_extender_11_out, bit_extender_12_out,
       bit_extender_13_out, bit_extender_14_out, bit_extender_15_out, bit_extender_16_out,
       bit_extender_17_out, bit_extender_18_out, bit_extender_19_out, bit_extender_20_out,
       bit_extender_21_out, bit_extender_22_out, bit_extender_23_out, bit_extender_24_out,
       bit_extender_25_out, bit_extender_26_out, bit_extender_29_out, bit_extender_30_out,
       bit_extender_31_out, bit_extender_32_out, bitextendall1sor0s_1_out_2, bitextendall1sor0s_2_out_2,
       bitextendall1sor0s_3_out_2, bitextendall1sor0s_4_out_2, bitextendall1sor0s_5_out_2,
       bitextendall1sor0s_6_out_2, bitextendall1sor0s_7_out_2, bitextendall1sor0s_8_out_2,
       bitextendall1sor0s_9_out_2, bitextendall1sor0s_10_out_2, buffer_1_out, counter_1_q, decoder_1_out0,
       divider_1_rem, divider_2_rem, divider_9_rem, divider_10_out, divider_11_out, even_parity_1_out,
       fpadder_1_out, fpadder_2_out, fpadder_4_out, fpadder_5_out, fpdivider_1_out, fpdivider_3_out,
       fpmultiplier_1_out, fpmultiplier_2_out, fpmultiplier_3_out, fpmultiplier_4_out, fpmultiplier_5_out,
       fpmultiplier_6_out, fpmultiplier_7_out, fpmultiplier_8_out, fpmultiplier_9_out, fpmultiplier_10_out,
       fpmultiplier_11_out, fpmultiplier_12_out, fpmultiplier_13_out, fpmultiplier_14_out,
       fpmultiplier_15_out, fpnegator_1_p2, fpnegator_2_p4, fpsubtractor_1_out, fpsubtractor_2_out,
       fptoint_1_p2, fptoint_3_p1, inttofp_3_p2, inttofp_4_p1, multiplexer_2_out, multiplexer_3_out,
       multiplexer_4_out, multiplexer_5_out, multiplexer_6_out, multiplexer_7_out, multiplexer_8_out,
       multiplexer_9_out, multiplier_1_out, multiplier_2_out, multiplier_3_out, multiplier_4_out,
       multiplier_5_out, multiplier_6_out, multiplier_13_out, multiplier_14_out, multiplier_15_out,
       multiplier_16_out, multiplier_17_out, multiplier_18_out, multiplier_19_out, multiplier_20_out,
       multiplier_21_out, multiplier_22_out, multiplier_23_out, multiplier_24_out, multiplier_25_out,
       multiplier_26_out, nand_1_out, negator_1_out, negator_2_out, nor_1_out, not_1_out, odd_parity_1_out,
       or_1_out, or_2_out, or_3_out, or_4_out, or_5_out, or_6_out, or_7_out, rom_1_data, rom_2_data,
       shifter_1_out, shifter_2_out, shifter_3_out, shifter_4_out, shifter_5_out, shifter_6_out,
       shifter_7_out, shifter_8_out, subtractor_7_out, subtractor_8_out, subtractor_9_out, xnor_1_out,
       xor_1_out;
  wire [31:0] fpadder_3_out, inttofp_1_p2, inttofp_2_p2, random_1_out;

  Counter #(.max('hffff), .width(16)) counter_1 (
    .up(1'b1), .count(clockCTR), .clk(clockCTR), .Q(counter_1_q));  // open: clr, load, D, carry
  Priority_Encoder #(.select(4)) priority_encoder_1 (
    .in0(in1[0]), .in1(in1[1]), .in2(in1[2]), .in3(in1[3]), .in4(in1[4]), .in5(in1[5]), .in6(in1[6]),
    .in7(in1[7]), .in8(in1[8]), .in9(in1[9]), .in10(in1[10]), .in11(in1[11]), .in12(in1[12]), .in13(in1[13]),
    .in14(in1[14]), .in15(in1[15]), .out(priority_encoder_1_out), .gs(priority_encoder_1_gs));  // open: en_out, en_in
  assign buffer_1_out = in1;  // Buffer buffer_1, 16 bits wide
  Adder #(.width(16)) adder_1 (.a(in1), .b(16'h5a), .out(adder_1_out));  // open: cin, cout
  Bit_Extender #(.in_width(16), .out_width(13), .\type ("zero")) bit_extender_1 (.in(in1), .out(bit_extender_1_out));
  nibblifySingleInput nibblifysingleinput_1 (
    .in_1(in1), .out_2(nibblifysingleinput_1_out_2), .out_3(nibblifysingleinput_1_out_3),
    .out_4(nibblifysingleinput_1_out_4), .out_5(nibblifysingleinput_1_out_5));
  assign and_1_out = in2 & ~16'hfff0;  // AND_Gate and_1, 16 bits wide
  assign and_2_out = in2 & ~16'hfff0;  // AND_Gate and_2, 16 bits wide
  assign and_3_out = in2 & ~16'hfff0;  // AND_Gate and_3, 16 bits wide
  Bit_Extender #(.in_width(16), .out_width(4), .\type ("zero")) bit_extender_2 (.in(in1), .out(bit_extender_2_out));
  Multiplier #(.width(16)) multiplier_1 (.a(in1), .b(in1), .out(multiplier_1_out));  // open: cin, cout
  Multiplier #(.mode("twosComplement"), .width(16)) multiplier_2 (
    .a(in1), .b(in1), .out(multiplier_2_out));  // open: cin, cout
  Multiplier #(.width(16)) multiplier_3 (.a(in1), .b(in1), .out(multiplier_3_out));  // open: cin, cout
  Multiplier #(.mode("twosComplement"), .width(16)) multiplier_4 (
    .a(in1), .b(in1), .out(multiplier_4_out));  // open: cin, cout
  FPMultiplier #(.fpwidth(16)) fpmultiplier_1 (.a(in1), .b(in1), .out(fpmultiplier_1_out));
  FPMultiplier #(.fpwidth(16)) fpmultiplier_2 (.a(in1), .b(in1), .out(fpmultiplier_2_out));
  ROM #(.addrWidth(16), .dataWidth(16)) rom_1 (.addr(divider_1_rem), .data(rom_1_data));
  Divider #(.width(16)) divider_1 (.a(in1), .b(16'h168), .rem(divider_1_rem));  // open: out, upper
  ROM #(.addrWidth(16), .dataWidth(16)) rom_2 (.addr(divider_2_rem), .data(rom_2_data));
  Divider #(.width(16)) divider_2 (.a(adder_1_out), .b(16'h168), .rem(divider_2_rem));  // open: out, upper
  assign not_1_out = ~in1;  // NOT_Gate not_1, 16 bits wide
  Random #(.seed(-559038737), .width(32)) random_1 (.next(clock), .clk(clock), .out(random_1_out));  // open: clr
  // Binary_to_BCD_converter #(.binvalue(13)) binary_to_bcd_converter_1: pin names not known; wires that end beside it: bit_extender_1_out, binary_to_bcd_converter_1_p2, binary_to_bcd_converter_1_p3, binary_to_bcd_converter_1_p4
  Bit_Extender #(.out_width(7), .\type ("zero")) bit_extender_3 (.in(in1[7:0]), .out(bit_extender_3_out));
  Bit_Extender #(.out_width(7), .\type ("zero")) bit_extender_4 (.in(in1[15:8]), .out(bit_extender_4_out));
  // IntToFP #(.width(16)) inttofp_1: pin names not known; wires that end beside it: in1, inttofp_1_p2
  // IntToFP #(.width(16)) inttofp_2: pin names not known; wires that end beside it: in2, inttofp_2_p2
  Multiplier #(.width(16)) multiplier_5 (.a(in1), .b(in1), .out(multiplier_5_out));  // open: cin, cout
  Multiplier #(.mode("twosComplement"), .width(16)) multiplier_6 (
    .a(in1), .b(in1), .out(multiplier_6_out));  // open: cin, cout
  FPMultiplier #(.fpwidth(16)) fpmultiplier_3 (.a(in1), .b(in1), .out(fpmultiplier_3_out));
  nibbleIfy nibbleify_1 (
    .in1(in1), .in2(in2), .out_3(nibbleify_1_out_3), .out_4(nibbleify_1_out_4), .out_5(nibbleify_1_out_5),
    .out_6(nibbleify_1_out_6), .out_7(nibbleify_1_out_7), .out_8(nibbleify_1_out_8),
    .out_9(nibbleify_1_out_9), .out_10(nibbleify_1_out_10));
  Adder #(.width(4)) adder_2 (.a(nibbleify_1_out_3), .b(nibbleify_1_out_4), .out(adder_2_out));  // open: cin, cout
  Adder #(.width(4)) adder_3 (.a(nibbleify_1_out_5), .b(nibbleify_1_out_6), .out(adder_3_out));  // open: cin, cout
  Adder #(.width(4)) adder_4 (.a(nibbleify_1_out_7), .b(nibbleify_1_out_8), .out(adder_4_out));  // open: cin, cout
  Adder #(.width(4)) adder_5 (.a(nibbleify_1_out_9), .b(nibbleify_1_out_10), .out(adder_5_out));  // open: cin, cout
  nibbleIfy nibbleify_2 (
    .in1(in1), .in2(in2), .out_3(nibbleify_2_out_3), .out_4(nibbleify_2_out_4), .out_5(nibbleify_2_out_5),
    .out_6(nibbleify_2_out_6), .out_7(nibbleify_2_out_7), .out_8(nibbleify_2_out_8),
    .out_9(nibbleify_2_out_9), .out_10(nibbleify_2_out_10));
  Subtractor #(.width(4)) subtractor_1 (
    .a(nibbleify_2_out_3), .b(nibbleify_2_out_4), .out(subtractor_1_out));  // open: bin, bout
  Subtractor #(.width(4)) subtractor_2 (
    .a(nibbleify_2_out_5), .b(nibbleify_2_out_6), .out(subtractor_2_out));  // open: bin, bout
  Subtractor #(.width(4)) subtractor_3 (
    .a(nibbleify_2_out_7), .b(nibbleify_2_out_8), .out(subtractor_3_out));  // open: bin, bout
  Subtractor #(.width(4)) subtractor_4 (
    .a(nibbleify_2_out_9), .b(nibbleify_2_out_10), .out(subtractor_4_out));  // open: bin, bout
  nibbleIfy nibbleify_3 (
    .in1(in1), .in2(in2), .out_3(nibbleify_3_out_3), .out_4(nibbleify_3_out_4), .out_5(nibbleify_3_out_5),
    .out_6(nibbleify_3_out_6), .out_7(nibbleify_3_out_7), .out_8(nibbleify_3_out_8),
    .out_9(nibbleify_3_out_9), .out_10(nibbleify_3_out_10));
  Multiplier #(.width(4)) multiplier_7 (
    .a(nibbleify_3_out_3), .b(nibbleify_3_out_4), .out(multiplier_7_out));  // open: cin, cout
  Multiplier #(.width(4)) multiplier_8 (
    .a(nibbleify_3_out_5), .b(nibbleify_3_out_6), .out(multiplier_8_out));  // open: cin, cout
  Multiplier #(.width(4)) multiplier_9 (
    .a(nibbleify_3_out_7), .b(nibbleify_3_out_8), .out(multiplier_9_out));  // open: cin, cout
  Multiplier #(.width(4)) multiplier_10 (
    .a(nibbleify_3_out_9), .b(nibbleify_3_out_10), .out(multiplier_10_out));  // open: cin, cout
  nibbleIfy nibbleify_4 (
    .in1(in1), .in2(in2), .out_3(nibbleify_4_out_3), .out_4(nibbleify_4_out_4), .out_5(nibbleify_4_out_5),
    .out_6(nibbleify_4_out_6), .out_7(nibbleify_4_out_7), .out_8(nibbleify_4_out_8),
    .out_9(nibbleify_4_out_9), .out_10(nibbleify_4_out_10));
  Divider #(.width(4)) divider_3 (
    .a(nibbleify_4_out_3), .b(nibbleify_4_out_4), .out(divider_3_out));  // open: upper, rem
  Divider #(.width(4)) divider_4 (
    .a(nibbleify_4_out_5), .b(nibbleify_4_out_6), .out(divider_4_out));  // open: upper, rem
  Divider #(.width(4)) divider_5 (
    .a(nibbleify_4_out_7), .b(nibbleify_4_out_8), .out(divider_5_out));  // open: upper, rem
  Divider #(.width(4)) divider_6 (
    .a(nibbleify_4_out_9), .b(nibbleify_4_out_10), .out(divider_6_out));  // open: upper, rem
  nibblifySingleInput nibblifysingleinput_2 (
    .in_1(in1), .out_2(nibblifysingleinput_2_out_2), .out_3(nibblifysingleinput_2_out_3),
    .out_4(nibblifysingleinput_2_out_4), .out_5(nibblifysingleinput_2_out_5));
  Adder #(.width(4)) adder_6 (
    .a(nibblifysingleinput_2_out_2), .b(nibblifysingleinput_2_out_3), .out(adder_6_out));  // open: cin, cout
  Adder #(.width(4)) adder_7 (
    .a(nibblifysingleinput_2_out_4), .b(nibblifysingleinput_2_out_5), .out(adder_7_out));  // open: cin, cout
  nibblifySingleInput nibblifysingleinput_3 (
    .in_1(in1), .out_2(nibblifysingleinput_3_out_2), .out_3(nibblifysingleinput_3_out_3),
    .out_4(nibblifysingleinput_3_out_4), .out_5(nibblifysingleinput_3_out_5));
  Subtractor #(.width(4)) subtractor_5 (
    .a(nibblifysingleinput_3_out_2), .b(nibblifysingleinput_3_out_3), .out(subtractor_5_out));  // open: bin, bout
  Subtractor #(.width(4)) subtractor_6 (
    .a(nibblifysingleinput_3_out_4), .b(nibblifysingleinput_3_out_5), .out(subtractor_6_out));  // open: bin, bout
  nibblifySingleInput nibblifysingleinput_4 (
    .in_1(in1), .out_2(nibblifysingleinput_4_out_2), .out_3(nibblifysingleinput_4_out_3),
    .out_4(nibblifysingleinput_4_out_4), .out_5(nibblifysingleinput_4_out_5));
  Multiplier #(.width(4)) multiplier_11 (
    .a(nibblifysingleinput_4_out_2), .b(nibblifysingleinput_4_out_3), .out(multiplier_11_out));  // open: cin, cout
  Multiplier #(.width(4)) multiplier_12 (
    .a(nibblifysingleinput_4_out_4), .b(nibblifysingleinput_4_out_5), .out(multiplier_12_out));  // open: cin, cout
  nibblifySingleInput nibblifysingleinput_5 (
    .in_1(in1), .out_2(nibblifysingleinput_5_out_2), .out_3(nibblifysingleinput_5_out_3),
    .out_4(nibblifysingleinput_5_out_4), .out_5(nibblifysingleinput_5_out_5));
  Divider #(.width(4)) divider_7 (
    .a(nibblifysingleinput_5_out_2), .b(nibblifysingleinput_5_out_3), .out(divider_7_out));  // open: upper, rem
  Divider #(.width(4)) divider_8 (
    .a(nibblifysingleinput_5_out_4), .b(nibblifysingleinput_5_out_5), .out(divider_8_out));  // open: upper, rem
  Divider #(.width(16)) divider_9 (.a(in1), .b(in2), .rem(divider_9_rem));  // open: out, upper
  Multiplier #(.width(16)) multiplier_13 (.a(in1), .b(in1), .out(multiplier_13_out));  // open: cin, cout
  Multiplier #(.mode("twosComplement"), .width(16)) multiplier_14 (
    .a(in1), .b(in1), .out(multiplier_14_out));  // open: cin, cout
  FPMultiplier #(.fpwidth(16)) fpmultiplier_4 (.a(in1), .b(in1), .out(fpmultiplier_4_out));
  Multiplier #(.width(16)) multiplier_15 (.a(in1), .b(in1), .out(multiplier_15_out));  // open: cin, cout
  Multiplier #(.mode("twosComplement"), .width(16)) multiplier_16 (
    .a(in1), .b(in1), .out(multiplier_16_out));  // open: cin, cout
  FPMultiplier #(.fpwidth(16)) fpmultiplier_5 (.a(in1), .b(in1), .out(fpmultiplier_5_out));
  Comparator #(.mode("unsigned"), .width(16)) comparator_1 (
    .a(in1), .b(in2), .gt(comparator_1_gt), .eq(comparator_1_eq), .lt(comparator_1_lt));
  Comparator #(.width(16)) comparator_2 (.a(in1), .b(in2), .gt(comparator_2_gt), .lt(comparator_2_lt));  // open: eq
  // FPComparator #(.fpwidth(16)) fpcomparator_1: pin names not known; wires that end beside it: in1, in2, fpcomparator_1_p3, fpcomparator_1_p4, fpcomparator_1_p5
  Comparator #(.mode("unsigned"), .width(16)) comparator_3 (
    .a(in1), .b(in2), .gt(comparator_3_gt), .eq(comparator_3_eq), .lt(comparator_3_lt));
  Comparator #(.width(16)) comparator_4 (.a(in1), .b(in2), .gt(comparator_4_gt), .lt(comparator_4_lt));  // open: eq
  // FPComparator #(.fpwidth(16)) fpcomparator_2: pin names not known; wires that end beside it: in1, in2, fpcomparator_2_p3, fpcomparator_2_p4, fpcomparator_2_p5
  Subtractor #(.width(16)) subtractor_7 (.a(in1), .b(in2), .out(subtractor_7_out));  // open: bin, bout
  FPSubtractor #(.fpwidth(16)) fpsubtractor_1 (.a(in1), .b(in2), .out(fpsubtractor_1_out));
  Bit_Extender #(.in_width(16), .out_width(2), .\type ("zero")) bit_extender_5 (.in(in2), .out(bit_extender_5_out));
  assign and_4_out = in1 & ~16'hf;  // AND_Gate and_4, 16 bits wide
  assign or_1_out = and_4_out | and_5_out;  // OR_Gate or_1, 16 bits wide
  assign and_5_out = in2 & ~16'hfff0;  // AND_Gate and_5, 16 bits wide
  assign and_6_out = in1 & ~16'hf0;  // AND_Gate and_6, 16 bits wide
  assign or_2_out = and_6_out | shifter_1_out;  // OR_Gate or_2, 16 bits wide
  Shifter #(.width(16)) shifter_1 (.in(and_1_out), .\dist (4'b0100), .out(shifter_1_out));
  assign and_7_out = in1 & ~16'hf00;  // AND_Gate and_7, 16 bits wide
  assign or_3_out = and_7_out | shifter_2_out;  // OR_Gate or_3, 16 bits wide
  Shifter #(.width(16)) shifter_2 (.in(and_2_out), .\dist (4'b1000), .out(shifter_2_out));
  assign and_8_out = in1 & ~16'hf000;  // AND_Gate and_8, 16 bits wide
  assign or_4_out = and_8_out | shifter_3_out;  // OR_Gate or_4, 16 bits wide
  Shifter #(.width(16)) shifter_3 (.in(and_3_out), .\dist (4'b1011), .out(shifter_3_out));
  Decoder #(.enable("false"), .select(4)) decoder_1 (
    .out0(decoder_1_out0[0]), .out1(decoder_1_out0[1]), .out2(decoder_1_out0[2]), .out3(decoder_1_out0[3]),
    .out4(decoder_1_out0[4]), .out5(decoder_1_out0[5]), .out6(decoder_1_out0[6]), .out7(decoder_1_out0[7]),
    .out8(decoder_1_out0[8]), .out9(decoder_1_out0[9]), .out10(decoder_1_out0[10]),
    .out11(decoder_1_out0[11]), .out12(decoder_1_out0[12]), .out13(decoder_1_out0[13]),
    .out14(decoder_1_out0[14]), .out15(decoder_1_out0[15]), .sel(bit_extender_2_out));
  Adder #(.width(16)) adder_8 (.a(multiplier_1_out), .b(in2), .out(adder_8_out));  // open: cin, cout
  Adder #(.width(16)) adder_9 (.a(multiplier_2_out), .b(in2), .out(adder_9_out));  // open: cin, cout
  Multiplier #(.width(16)) multiplier_17 (.a(multiplier_3_out), .b(in1), .out(multiplier_17_out));  // open: cin, cout
  Multiplier #(.mode("twosComplement"), .width(16)) multiplier_18 (
    .a(multiplier_4_out), .b(in1), .out(multiplier_18_out));  // open: cin, cout
  FPMultiplier #(.fpwidth(16)) fpmultiplier_6 (.a(fpmultiplier_1_out), .b(in1), .out(fpmultiplier_6_out));
  FPMultiplier #(.fpwidth(16)) fpmultiplier_7 (.a(fpmultiplier_2_out), .b(in1), .out(fpmultiplier_7_out));
  assign bit_extender_6_out = {{3{priority_encoder_1_gs}}, priority_encoder_1_gs};  // Bit_Extender bit_extender_6
  assign bit_extender_7_out = {{8{1'b0}}, in1[7:0]};  // Bit_Extender bit_extender_7
  assign bit_extender_8_out = {{8{1'b0}}, in1[15:8]};  // Bit_Extender bit_extender_8
  Adder #(.width(16)) adder_10 (.a(in2), .b(in1), .out(adder_10_out));  // open: cin, cout
  Subtractor #(.width(16)) subtractor_8 (.a(in1), .b(in2), .out(subtractor_8_out));  // open: bin, bout
  Multiplier #(.width(16)) multiplier_19 (.a(in1), .b(in2), .out(multiplier_19_out));  // open: cin, cout
  Multiplier #(.mode("twosComplement"), .width(16)) multiplier_20 (
    .a(in1), .b(in2), .out(multiplier_20_out));  // open: cin, cout
  Divider #(.width(16)) divider_10 (.a(in1), .b(in2), .out(divider_10_out));  // open: upper, rem
  Divider #(.mode("twosComplement"), .width(16)) divider_11 (
    .a(in1), .b(in2), .out(divider_11_out));  // open: upper, rem
  Negator #(.width(16)) negator_1 (.in(in1), .out(negator_1_out));
  Shifter #(.width(16)) shifter_4 (.in(in1), .\dist (in2[3:0]), .out(shifter_4_out));
  // IntToFP #(.fpwidth(16), .width(16)) inttofp_3: pin names not known; wires that end beside it: in1, inttofp_3_p2
  FPAdder #(.fpwidth(16)) fpadder_1 (.a(in1), .b(in2), .out(fpadder_1_out));
  FPSubtractor #(.fpwidth(16)) fpsubtractor_2 (.a(in1), .b(in2), .out(fpsubtractor_2_out));
  FPMultiplier #(.fpwidth(16)) fpmultiplier_8 (.a(in1), .b(in2), .out(fpmultiplier_8_out));
  FPDivider #(.fpwidth(16)) fpdivider_1 (.a(in1), .b(in2), .out(fpdivider_1_out));
  // FPNegator #(.fpwidth(16)) fpnegator_1: pin names not known; wires that end beside it: in1, fpnegator_1_p2
  // FPToInt #(.fpwidth(16), .width(16)) fptoint_1: pin names not known; wires that end beside it: in1, fptoint_1_p2
  assign and_9_out = in1 & in2;  // AND_Gate and_9, 16 bits wide
  assign or_5_out = in1 | in2;  // OR_Gate or_5, 16 bits wide
  assign nand_1_out = ~(in1 & in2);  // NAND_Gate nand_1, 16 bits wide
  assign nor_1_out = ~(in1 | in2);  // NOR_Gate nor_1, 16 bits wide
  assign xor_1_out = in1 ^ in2;  // XOR_Gate xor_1, 16 bits wide
  assign xnor_1_out = ~(in1 ^ in2);  // XNOR_Gate xnor_1, 16 bits wide
  Shifter #(.shift("lr"), .width(16)) shifter_5 (.in(in1), .\dist (in2[3:0]), .out(shifter_5_out));
  Shifter #(.shift("ar"), .width(16)) shifter_6 (.in(in1), .\dist (in2[3:0]), .out(shifter_6_out));
  Shifter #(.shift("rl"), .width(16)) shifter_7 (.in(in1), .\dist (in2[3:0]), .out(shifter_7_out));
  Shifter #(.shift("rr"), .width(16)) shifter_8 (.in(in1), .\dist (in2[3:0]), .out(shifter_8_out));
  LED debug (.in(dipswitch_1_p1));
  // DipSwitch #(.number(1)) dipswitch_1: pin names not known; wires that end beside it: dipswitch_1_p1
  FPDivider #(.fpwidth(16)) fpdivider_2 (.a(in1), .b(in2));  // open: out
  // FPToInt #(.fpwidth(16), .width(32)) fptoint_2: pin names not known
  Adder #(.width(16)) adder_11 (.a(in1), .b(16'h1), .out(adder_11_out));  // open: cin, cout
  Adder #(.width(16)) adder_12 (.a(in1), .b({16{1'b1}}), .out(adder_12_out));  // open: cin, cout
  BitFinder #(.width(16)) bitfinder_1 (.in(in1), .index(bitfinder_1_index));  // open: found
  BitFinder #(.\type ("high1"), .width(16)) bitfinder_2 (.in(in1), .index(bitfinder_2_index));  // open: found
  BitFinder #(.\type ("low0"), .width(16)) bitfinder_3 (.in(in1), .index(bitfinder_3_index));  // open: found
  BitFinder #(.\type ("high0"), .width(16)) bitfinder_4 (.in(in1), .index(bitfinder_4_index));  // open: found
  Adder #(.width(7)) adder_13 (
    .a(bit_extender_3_out), .b(7'b0000001), .out(adder_13_out), .cout(adder_13_cout));  // open: cin
  Adder #(.width(7)) adder_14 (
    .a(bit_extender_4_out), .b({7{1'b0}}), .out(adder_14_out), .cin(adder_13_cout));  // open: cout
  assign even_parity_1_out = ~(in1 ^ in2);  // Even_Parity even_parity_1, 16 bits wide
  assign odd_parity_1_out = in1 ^ in2;  // Odd_Parity odd_parity_1, 16 bits wide
  BitAdder #(.width(16)) bitadder_1 (.in0(in1), .out(bitadder_1_out));
  BitAdder #(.width(32)) bitadder_2 (.in0({in2, in1}), .out(bitadder_2_out));
  FPAdder #(.fpwidth(16)) fpadder_2 (.a(in1), .b(in2), .out(fpadder_2_out));
  FPAdder fpadder_3 (.a(inttofp_1_p2), .b(inttofp_2_p2), .out(fpadder_3_out));
  Comparator #(.mode("unsigned"), .width(16)) comparator_5 (
    .a(in1), .b(in2), .gt(comparator_5_gt), .lt(comparator_5_lt));  // open: eq
  Comparator #(.width(16)) comparator_6 (.a(in1), .b(in2), .gt(comparator_6_gt), .lt(comparator_6_lt));  // open: eq
  // FPComparator #(.fpwidth(16)) fpcomparator_3: pin names not known; wires that end beside it: in1, in2, fpcomparator_3_p3, fpcomparator_3_p4
  Adder #(.width(16)) adder_15 (.a(in1), .b(in2), .out(adder_15_out), .cout(adder_15_cout));  // open: cin
  bitExtendAll1sor0s bitextendall1sor0s_1 (.in_1(adder_15_cout), .out_2(bitextendall1sor0s_1_out_2));
  Subtractor #(.width(16)) subtractor_9 (
    .a(in1), .b(in2), .out(subtractor_9_out), .bout(subtractor_9_bout));  // open: bin
  bitExtendAll1sor0s bitextendall1sor0s_2 (.in_1(subtractor_9_bout), .out_2(bitextendall1sor0s_2_out_2));
  Multiplier #(.width(16)) multiplier_21 (.a(multiplier_5_out), .b(in1), .out(multiplier_21_out));  // open: cin, cout
  Multiplier #(.mode("twosComplement"), .width(16)) multiplier_22 (
    .a(multiplier_6_out), .b(in1), .out(multiplier_22_out));  // open: cin, cout
  FPMultiplier #(.fpwidth(16)) fpmultiplier_9 (.a(fpmultiplier_3_out), .b(in1), .out(fpmultiplier_9_out));
  assign bit_extender_9_out = {{8{1'b0}}, {adder_7_out, adder_6_out}};  // Bit_Extender bit_extender_9
  assign bit_extender_10_out = {{8{1'b0}}, {subtractor_6_out, subtractor_5_out}};  // Bit_Extender bit_extender_10
  assign bit_extender_11_out = {{8{1'b0}}, {multiplier_12_out, multiplier_11_out}};  // Bit_Extender bit_extender_11
  assign bit_extender_12_out = {{8{1'b0}}, {divider_8_out, divider_7_out}};  // Bit_Extender bit_extender_12
  Multiplier #(.width(16)) multiplier_23 (.a(multiplier_15_out), .b(in1), .out(multiplier_23_out));  // open: cin, cout
  Multiplier #(.mode("twosComplement"), .width(16)) multiplier_24 (
    .a(multiplier_16_out), .b(in1), .out(multiplier_24_out));  // open: cin, cout
  FPMultiplier #(.fpwidth(16)) fpmultiplier_10 (.a(fpmultiplier_5_out), .b(in1), .out(fpmultiplier_10_out));
  assign bit_extender_13_out = {{15{1'b0}}, comparator_1_gt};  // Bit_Extender bit_extender_13
  assign bit_extender_14_out = {{15{1'b0}}, comparator_1_eq};  // Bit_Extender bit_extender_14
  assign bit_extender_15_out = {{15{1'b0}}, comparator_1_lt};  // Bit_Extender bit_extender_15
  assign bit_extender_16_out = {{15{1'b0}}, comparator_2_gt};  // Bit_Extender bit_extender_16
  assign bit_extender_17_out = {{15{1'b0}}, comparator_2_lt};  // Bit_Extender bit_extender_17
  assign bit_extender_18_out = {{15{1'b0}}, fpcomparator_1_p3};  // Bit_Extender bit_extender_18
  assign bit_extender_19_out = {{15{1'b0}}, fpcomparator_1_p4};  // Bit_Extender bit_extender_19
  assign bit_extender_20_out = {{15{1'b0}}, fpcomparator_1_p5};  // Bit_Extender bit_extender_20
  bitExtendAll1sor0s bitextendall1sor0s_3 (.in_1(comparator_3_gt), .out_2(bitextendall1sor0s_3_out_2));
  bitExtendAll1sor0s bitextendall1sor0s_4 (.in_1(comparator_3_eq), .out_2(bitextendall1sor0s_4_out_2));
  bitExtendAll1sor0s bitextendall1sor0s_5 (.in_1(comparator_3_lt), .out_2(bitextendall1sor0s_5_out_2));
  bitExtendAll1sor0s bitextendall1sor0s_6 (.in_1(comparator_4_gt), .out_2(bitextendall1sor0s_6_out_2));
  bitExtendAll1sor0s bitextendall1sor0s_7 (.in_1(comparator_4_lt), .out_2(bitextendall1sor0s_7_out_2));
  bitExtendAll1sor0s bitextendall1sor0s_8 (.in_1(fpcomparator_2_p3), .out_2(bitextendall1sor0s_8_out_2));
  bitExtendAll1sor0s bitextendall1sor0s_9 (.in_1(fpcomparator_2_p4), .out_2(bitextendall1sor0s_9_out_2));
  bitExtendAll1sor0s bitextendall1sor0s_10 (.in_1(fpcomparator_2_p5), .out_2(bitextendall1sor0s_10_out_2));
  bitchecker bitchecker_1 (.bitToCheck(16'hf), .bits(subtractor_7_out), .\bit (bitchecker_1_bit));
  Negator #(.width(16)) negator_2 (.in(subtractor_7_out), .out(negator_2_out));
  // FPComparator #(.fpwidth(16)) fpcomparator_4: pin names not known; wires that end beside it: fpcomparator_4_p1
  // FPNegator #(.fpwidth(16)) fpnegator_2: pin names not known; wires that end beside it: fpsubtractor_1_out, fpsubtractor_1_out, {16{1'b0}}, fpnegator_2_p4
  Multiplexer #(.select(2), .width(4)) multiplexer_1 (
    .in0(nibblifysingleinput_1_out_2), .in1(nibblifysingleinput_1_out_3), .in2(nibblifysingleinput_1_out_4),
    .in3(nibblifysingleinput_1_out_5), .out(multiplexer_1_out), .sel(bit_extender_5_out));
  Adder #(.width(16)) adder_16 (.a(multiplier_17_out), .b(in2), .out(adder_16_out));  // open: cin, cout
  Adder #(.width(16)) adder_17 (.a(multiplier_18_out), .b(in2), .out(adder_17_out));  // open: cin, cout
  FPAdder #(.fpwidth(16)) fpadder_4 (.a(fpmultiplier_6_out), .b(in2), .out(fpadder_4_out));
  FPMultiplier #(.fpwidth(16)) fpmultiplier_11 (.a(fpmultiplier_7_out), .b(in1), .out(fpmultiplier_11_out));
  FPAdder #(.fpwidth(16)) fpadder_5 (.a(fpmultiplier_11_out), .b(in2), .out(fpadder_5_out));
  Bit_Extender #(.in_width(32), .\type ("zero")) bit_extender_21 (.in(random_1_out), .out(bit_extender_21_out));
  assign bit_extender_22_out = {{15{dipswitch_1_p1}}, dipswitch_1_p1};  // Bit_Extender bit_extender_22
  // IntToFP #(.fpwidth(16), .width(32)) inttofp_4: pin names not known; wires that end beside it: inttofp_4_p1, inttofp_4_p2
  assign bit_extender_23_out = {{12{1'b0}}, bitfinder_1_index};  // Bit_Extender bit_extender_23
  assign bit_extender_24_out = {{12{1'b0}}, bitfinder_2_index};  // Bit_Extender bit_extender_24
  assign bit_extender_25_out = {{12{1'b0}}, bitfinder_3_index};  // Bit_Extender bit_extender_25
  assign bit_extender_26_out = {{12{1'b0}}, bitfinder_4_index};  // Bit_Extender bit_extender_26
  assign bit_extender_27_out = {{1{1'b0}}, adder_13_out};  // Bit_Extender bit_extender_27
  assign bit_extender_28_out = {{1{1'b0}}, adder_14_out};  // Bit_Extender bit_extender_28
  assign bit_extender_29_out = {{11{1'b0}}, bitadder_1_out};  // Bit_Extender bit_extender_29
  assign bit_extender_30_out = {{10{1'b0}}, bitadder_2_out};  // Bit_Extender bit_extender_30
  FPDivider #(.fpwidth(16)) fpdivider_3 (.a(fpadder_2_out), .b(16'h4000), .out(fpdivider_3_out));
  FPDivider fpdivider_4 (.a(fpadder_3_out), .b(32'h40000000));  // open: out
  Multiplexer #(.width(16)) multiplexer_2 (.in0(in1), .in1(in2), .out(multiplexer_2_out), .sel(comparator_5_gt));
  Multiplexer #(.width(16)) multiplexer_3 (.in0(in1), .in1(in2), .out(multiplexer_3_out), .sel(comparator_5_lt));
  Multiplexer #(.width(16)) multiplexer_4 (.in0(in1), .in1(in2), .out(multiplexer_4_out), .sel(comparator_6_gt));
  Multiplexer #(.width(16)) multiplexer_5 (.in0(in1), .in1(in2), .out(multiplexer_5_out), .sel(comparator_6_lt));
  Multiplexer #(.width(16)) multiplexer_6 (.in0(in1), .in1(in2), .out(multiplexer_6_out), .sel(fpcomparator_3_p3));
  Multiplexer #(.width(16)) multiplexer_7 (.in0(in1), .in1(in2), .out(multiplexer_7_out), .sel(fpcomparator_3_p4));
  assign or_6_out = adder_15_out | bitextendall1sor0s_1_out_2;  // OR_Gate or_6, 16 bits wide
  assign or_7_out = subtractor_9_out | bitextendall1sor0s_2_out_2;  // OR_Gate or_7, 16 bits wide
  assign and_10_out = in1 & ~in2;  // AND_Gate and_10, 16 bits wide
  Multiplier #(.width(16)) multiplier_25 (.a(multiplier_23_out), .b(in1), .out(multiplier_25_out));  // open: cin, cout
  Multiplier #(.mode("twosComplement"), .width(16)) multiplier_26 (
    .a(multiplier_24_out), .b(in1), .out(multiplier_26_out));  // open: cin, cout
  FPMultiplier #(.fpwidth(16)) fpmultiplier_12 (.a(fpmultiplier_10_out), .b(in1), .out(fpmultiplier_12_out));
  Multiplexer #(.width(16)) multiplexer_8 (
    .in0(subtractor_7_out), .in1(negator_2_out), .out(multiplexer_8_out), .sel(bitchecker_1_bit));
  Multiplexer #(.width(16)) multiplexer_9 (
    .in0(fpsubtractor_1_out), .in1(fpnegator_2_p4), .out(multiplexer_9_out), .sel(fpcomparator_4_p1));
  assign bit_extender_31_out = {{12{1'b0}}, multiplexer_1_out};  // Bit_Extender bit_extender_31
  assign bit_extender_32_out = {{12{1'b0}}, and_11_out};  // Bit_Extender bit_extender_32
  assign and_11_out = priority_encoder_1_out & bit_extender_6_out;  // AND_Gate and_11, 4 bits wide
  assign and_12_out = in2 & bit_extender_22_out;  // AND_Gate and_12, 16 bits wide
  FPMultiplier #(.fpwidth(16)) fpmultiplier_13 (.a(inttofp_4_p1), .b(in2), .out(fpmultiplier_13_out));
  // FPToInt #(.width(16)) fptoint_3: pin names not known; wires that end beside it: fptoint_3_p1
  FPMultiplier #(.fpwidth(16)) fpmultiplier_14 (.a(rom_1_data), .b(in2), .out(fpmultiplier_14_out));
  FPMultiplier #(.fpwidth(16)) fpmultiplier_15 (.a(rom_2_data), .b(in2), .out(fpmultiplier_15_out));
  Multiplexer #(.select(7), .width(16)) multiplexer_10 (
    .in0(adder_10_out), .in1(subtractor_8_out), .in2(multiplier_19_out), .in3(multiplier_20_out),
    .in4(divider_10_out), .in5(divider_11_out), .in6(negator_1_out), .in7(shifter_4_out), .in8(inttofp_3_p2),
    .in9(fpadder_1_out), .in10(fpsubtractor_2_out), .in11(fpmultiplier_8_out), .in12(fpdivider_1_out),
    .in13(fpnegator_1_p2), .in14(fptoint_1_p2), .in15(not_1_out), .in16(and_9_out), .in17(or_5_out),
    .in18(nand_1_out), .in19(nor_1_out), .in20(xor_1_out), .in21(xnor_1_out), .in22(RAMIn),
    .in23(shifter_5_out), .in24(shifter_6_out), .in25(shifter_7_out), .in26(shifter_8_out),
    .in27(bit_extender_21_out),
    .in28({binary_to_bcd_converter_1_p2, binary_to_bcd_converter_1_p3, binary_to_bcd_converter_1_p4, inttofp_4_p2}),
    .in29(and_12_out), .in30(fpmultiplier_13_out), .in31(adder_11_out), .in32(adder_12_out),
    .in33(bit_extender_23_out), .in34(bit_extender_24_out), .in35(bit_extender_25_out),
    .in36(bit_extender_26_out), .in37({bit_extender_28_out, bit_extender_27_out}), .in38(even_parity_1_out),
    .in39(odd_parity_1_out), .in40(bit_extender_29_out), .in41(bit_extender_30_out), .in42(fpdivider_3_out),
    .in43(fptoint_3_p1), .in44(multiplexer_2_out), .in45(multiplexer_3_out), .in46(multiplexer_4_out),
    .in47(multiplexer_5_out), .in48(multiplexer_6_out), .in49(multiplexer_7_out), .in50(or_7_out),
    .in51(and_10_out), .in52({in1[7:0], in1[15:8]}), .in53(multiplier_21_out), .in54(multiplier_22_out),
    .in55(fpmultiplier_9_out), .in56(or_6_out), .in57({adder_5_out, adder_4_out, adder_3_out, adder_2_out}),
    .in58({subtractor_4_out, subtractor_3_out, subtractor_2_out, subtractor_1_out}),
    .in59({multiplier_10_out, multiplier_9_out, multiplier_8_out, multiplier_7_out}),
    .in60({divider_6_out, divider_5_out, divider_4_out, divider_3_out}), .in61(bit_extender_9_out),
    .in62(bit_extender_10_out), .in63(bit_extender_11_out), .in64(bit_extender_12_out), .in65(divider_9_rem),
    .in66(multiplier_13_out), .in67(multiplier_14_out), .in68(fpmultiplier_4_out), .in69(multiplier_25_out),
    .in70(multiplier_26_out), .in71(fpmultiplier_12_out), .in72(bit_extender_13_out),
    .in73(bit_extender_14_out), .in74(bit_extender_15_out), .in75(16'hbeef), .in76(bit_extender_16_out),
    .in77(bit_extender_17_out), .in78(bit_extender_18_out), .in79(bit_extender_19_out),
    .in80(bit_extender_20_out), .in81(bitextendall1sor0s_3_out_2), .in82(bitextendall1sor0s_4_out_2),
    .in83(bitextendall1sor0s_5_out_2), .in84(bitextendall1sor0s_6_out_2), .in85(bitextendall1sor0s_7_out_2),
    .in86(bitextendall1sor0s_8_out_2), .in87(bitextendall1sor0s_9_out_2), .in88(bitextendall1sor0s_10_out_2),
    .in89(multiplexer_8_out), .in90(multiplexer_9_out), .in91(bit_extender_31_out), .in92(or_1_out),
    .in93(or_2_out), .in94(or_3_out), .in95(or_4_out), .in96(counter_1_q), .in97(decoder_1_out0),
    .in98(adder_8_out), .in99(adder_9_out), .in100(adder_16_out), .in101(adder_17_out),
    .in102(fpadder_4_out), .in103(fpadder_5_out), .in104(bit_extender_32_out), .in105(buffer_1_out),
    .in106(16'h4248), .in107(16'h3e79), .in108(fpmultiplier_14_out), .in109(fpmultiplier_15_out),
    .in110(ascii), .in111(bit_extender_7_out), .in112(bit_extender_8_out), .out(value), .sel(opcode));  // open: in113, in114, in115, in116, in117, in118, in119, in120, in121, in122, in123, in124, in125, in126, in127

  // Notes on the sheet:
  //   contents of rom_1 (hex, n*v repeats v):
  //   0 2478 2878 2ab3 2c77 2d94 2eb1 2fcd 3074 3102 318f 321b 32a7 3333 33be 3424 3469 34ae 34f2 3536
  //   3579 35bc 35fe 3640 3682 36c3 3704 3744 3783 37c2 3800 381f 383d 385b 3879 3897 38b4 38d1 38ed 3909
  //   3924 3940 395a 3975 398f 39a8 39c1 39da 39f2 3a0a 3a21 3a38 3a4e 3a64 3a79 3a8e 3aa2 3ab6 3ac9 3adb
  //   3aee 3aff 3b10 3b21 3b31 3b40 3b4f 3b5d 3b6b 3b78 3b84 3b90 3b9c 3ba7 3bb1 3bba 3bc3 3bcc 3bd3 3bda
  //   3be1 3be7 3bec 3bf1 3bf5 3bf8 3bfb 3bfd 3bff 3c00 3c00 3c00 3bff 3bfd 3bfb 3bf8 3bf5 3bf1 3bec 3be7
  //   3be1 3bda 3bd3 3bcc 3bc3 3bba 3bb1 3ba7 3b9c 3b90 3b84 3b78 3b6b 3b5d 3b4f 3b40 3b31 3b21 3b10 3aff
  //   3aee 3adb 3ac9 3ab6 3aa2 3a8e 3a79 3a64 3a4e 3a38 3a21 3a0a 39f2 39da 39c1 39a8 398f 3975 395a 3940
  //   3924 3909 38ed 38d1 38b4 3897 3879 385b 383d 381f 3800 37c2 3783 3744 3704 36c3 3682 3640 35fe 35bc
  //   3579 3536 34f2 34ae 3469 3424 33be 3333 32a7 321b 318f 3102 3074 2fcd 2eb1 2d94 2c77 2ab3 2878 2478
  //   8 a478 a878 aab3 ac77 ad94 aeb1 afcd b074 b102 b18f b21b b2a7 b333 b3be b424 b469 b4ae b4f2 b536
  //   b579 b5bc b5fe b640 b682 b6c3 b704 b744 b783 b7c2 b800 b81f b83d b85b b879 b897 b8b4 b8d1 b8ed b909
  //   b924 b940 b95a b975 b98f b9a8 b9c1 b9da b9f2 ba0a ba21 ba38 ba4e ba64 ba79 ba8e baa2 bab6 bac9 badb
  //   baee baff bb10 bb21 bb31 bb40 bb4f bb5d bb6b bb78 bb84 bb90 bb9c bba7 bbb1 bbba bbc3 bbcc bbd3 bbda
  //   bbe1 bbe7 bbec bbf1 bbf5 bbf8 bbfb bbfd bbff bc00 bc00 bc00 bbff bbfd bbfb bbf8 bbf5 bbf1 bbec bbe7
  //   bbe1 bbda bbd3 bbcc bbc3 bbba bbb1 bba7 bb9c bb90 bb84 bb78 bb6b bb5d bb4f bb40 bb31 bb21 bb10 baff
  //   baee badb bac9 bab6 baa2 ba8e ba79 ba64 ba4e ba38 ba21 ba0a b9f2 b9da b9c1 b9a8 b98f b975 b95a b940
  //   b924 b909 b8ed b8d1 b8b4 b897 b879 b85b b83d b81f b800 b7c2 b783 b744 b704 b6c3 b682 b640 b5fe b5bc
  //   b579 b536 b4f2 b4ae b469 b424 b3be b333 b2a7 b21b b18f b102 b074 afcd aeb1 ad94 ac77 aab3 a878 a478
  //   contents of rom_2 (hex, n*v repeats v):
  //   0 2478 2878 2ab3 2c77 2d94 2eb1 2fcd 3074 3102 318f 321b 32a7 3333 33be 3424 3469 34ae 34f2 3536
  //   3579 35bc 35fe 3640 3682 36c3 3704 3744 3783 37c2 3800 381f 383d 385b 3879 3897 38b4 38d1 38ed 3909
  //   3924 3940 395a 3975 398f 39a8 39c1 39da 39f2 3a0a 3a21 3a38 3a4e 3a64 3a79 3a8e 3aa2 3ab6 3ac9 3adb
  //   3aee 3aff 3b10 3b21 3b31 3b40 3b4f 3b5d 3b6b 3b78 3b84 3b90 3b9c 3ba7 3bb1 3bba 3bc3 3bcc 3bd3 3bda
  //   3be1 3be7 3bec 3bf1 3bf5 3bf8 3bfb 3bfd 3bff 3c00 3c00 3c00 3bff 3bfd 3bfb 3bf8 3bf5 3bf1 3bec 3be7
  //   3be1 3bda 3bd3 3bcc 3bc3 3bba 3bb1 3ba7 3b9c 3b90 3b84 3b78 3b6b 3b5d 3b4f 3b40 3b31 3b21 3b10 3aff
  //   3aee 3adb 3ac9 3ab6 3aa2 3a8e 3a79 3a64 3a4e 3a38 3a21 3a0a 39f2 39da 39c1 39a8 398f 3975 395a 3940
  //   3924 3909 38ed 38d1 38b4 3897 3879 385b 383d 381f 3800 37c2 3783 3744 3704 36c3 3682 3640 35fe 35bc
  //   3579 3536 34f2 34ae 3469 3424 33be 3333 32a7 321b 318f 3102 3074 2fcd 2eb1 2d94 2c77 2ab3 2878 2478
  //   8 a478 a878 aab3 ac77 ad94 aeb1 afcd b074 b102 b18f b21b b2a7 b333 b3be b424 b469 b4ae b4f2 b536
  //   b579 b5bc b5fe b640 b682 b6c3 b704 b744 b783 b7c2 b800 b81f b83d b85b b879 b897 b8b4 b8d1 b8ed b909
  //   b924 b940 b95a b975 b98f b9a8 b9c1 b9da b9f2 ba0a ba21 ba38 ba4e ba64 ba79 ba8e baa2 bab6 bac9 badb
  //   baee baff bb10 bb21 bb31 bb40 bb4f bb5d bb6b bb78 bb84 bb90 bb9c bba7 bbb1 bbba bbc3 bbcc bbd3 bbda
  //   bbe1 bbe7 bbec bbf1 bbf5 bbf8 bbfb bbfd bbff bc00 bc00 bc00 bbff bbfd bbfb bbf8 bbf5 bbf1 bbec bbe7
  //   bbe1 bbda bbd3 bbcc bbc3 bbba bbb1 bba7 bb9c bb90 bb84 bb78 bb6b bb5d bb4f bb40 bb31 bb21 bb10 baff
  //   baee badb bac9 bab6 baa2 ba8e ba79 ba64 ba4e ba38 ba21 ba0a b9f2 b9da b9c1 b9a8 b98f b975 b95a b940
  //   b924 b909 b8ed b8d1 b8b4 b897 b879 b85b b83d b81f b800 b7c2 b783 b744 b704 b6c3 b682 b640 b5fe b5bc
  //   b579 b536 b4f2 b4ae b469 b424 b3be b333 b2a7 b21b b18f b102 b074 afcd aeb1 ad94 ac77 aab3 a878 a478
  //   ^ returns PI in half precision floating point
  //   ^ returns PhI in half precision floating point
  //   looks kinda like a rocket ship
  //   ^this is cosine, which is just sine offset 90 degrees
  //   ^this is sine. i would use taylor series, but i have found it suprisingly hard to find something implementable. (and i'm not sure the numbers needed can be represented)
endmodule

module ALUInputAdapter (
  input  [15:0] in1,
  input  [15:0] in2,
  input  [15:0] regIn1,
  input  [15:0] regIn2,
  input  [7:0] ConstByte,
  output [15:0] out1,
  output [15:0] out2
);

  Multiplexer #(.width(16)) multiplexer_1 (.in0(in1), .in1(regIn1), .out(out1), .sel(ConstByte[0]));
  Multiplexer #(.width(16)) multiplexer_2 (.in0(in2), .in1(regIn2), .out(out2), .sel(ConstByte[1]));
endmodule

module BLU (
  input  [15:0] in1,
  input  [15:0] in2,
  input  update,
  input  [3:0] opcode,
  input  clock,
  output jump,
  output [15:0] RAMOut,
  output asciiEnable,
  output [15:0] asciiOut,
  output clear
);

  wire and_2_out, bit_bit, comparator_1_eq, comparator_1_gt, comparator_1_lt, comparator_2_gt,
       comparator_2_lt, comparator_3_eq, comparator_5_eq, fpcomparator_1_p3, fpcomparator_1_p4,
       fpcomparator_1_p5, not_1_out;

  Comparator #(.mode("unsigned"), .width(16)) comparator_1 (
    .a(in1), .b(in2), .gt(comparator_1_gt), .eq(comparator_1_eq), .lt(comparator_1_lt));
  Comparator #(.width(16)) comparator_2 (.a(in1), .b(in2), .gt(comparator_2_gt), .lt(comparator_2_lt));  // open: eq
  // FPComparator #(.fpwidth(16)) fpcomparator_1: pin names not known; wires that end beside it: in1, in2, fpcomparator_1_p3, fpcomparator_1_p4, fpcomparator_1_p5
  bitchecker \bit  (.bitToCheck(in2), .bits(in1), .\bit (bit_bit));
  and and_1 (asciiEnable, comparator_3_eq, update);
  RAM #(.addrWidth(16), .dataWidth(16)) DataRAM (
    .addr(in1), .we(and_2_out), .oe(1'b1), .clk(clock), .din(in2), .dout(RAMOut));
  Comparator #(.mode("unsigned"), .width(4)) comparator_3 (
    .a(opcode), .b(4'b1101), .eq(comparator_3_eq));  // open: gt, lt
  Comparator #(.mode("unsigned"), .width(4)) comparator_4 (.a(opcode), .b(4'b1100), .eq(clear));  // open: gt, lt
  Multiplexer #(.enable("true"), .select(4)) multiplexer_1 (
    .in0(comparator_1_gt), .in1(comparator_1_eq), .in2(comparator_1_lt), .in3(comparator_2_gt),
    .in4(comparator_2_lt), .in5(fpcomparator_1_p3), .in6(fpcomparator_1_p5), .in7(1'b1), .in8(1'b0),
    .in9(1'b0), .in10(bit_bit), .in11(fpcomparator_1_p4), .in12(not_1_out), .in13(1'b0), .in14(1'b0),
    .in15(1'b0), .out(jump), .sel(opcode), .en(update));
  not not_1 (not_1_out, bit_bit);
  Comparator #(.mode("unsigned"), .width(4)) comparator_5 (
    .a(opcode), .b(4'b1001), .eq(comparator_5_eq));  // open: gt, lt
  and and_2 (and_2_out, comparator_5_eq, update);

  assign asciiOut = in1;

  // Notes on the sheet:
  //   yes, i put the RAM in the BLU.
endmodule

module PPU (
  input  WriteToSprite,
  input  [7:0] SpriteNum,
  input  [15:0] address,
  input  [23:0] color
);

  RAM #(.addrWidth(7), .dataWidth(24)) ram_1 ();  // open: addr, we, oe, clk, din, dout
  RAM #(.addrWidth(7), .dataWidth(24)) ram_2 ();  // open: addr, we, oe, clk, din, dout
  RAM #(.addrWidth(7), .dataWidth(24)) ram_3 ();  // open: addr, we, oe, clk, din, dout
  RAM #(.addrWidth(7), .dataWidth(24)) ram_4 ();  // open: addr, we, oe, clk, din, dout
  RAM #(.addrWidth(7), .dataWidth(24)) ram_5 ();  // open: addr, we, oe, clk, din, dout
endmodule

module megaOR (
  input  [15:0] in_1,
  output out_2
);

  wire [1:0] or_3_out;
  wire [3:0] or_2_out;
  wire [7:0] or_1_out;

  assign or_1_out = in_1[7:0] | in_1[15:8];  // OR_Gate or_1, 8 bits wide
  assign or_2_out = or_1_out[3:0] | or_1_out[7:4];  // OR_Gate or_2, 4 bits wide
  assign or_3_out = or_2_out[1:0] | or_2_out[3:2];  // OR_Gate or_3, 2 bits wide
  or or_4 (out_2, or_3_out[0], or_3_out[1]);
endmodule

module bitchecker (
  input  [15:0] bits,
  input  [15:0] bitToCheck,
  output \bit 
);

  wire [3:0] bit_extender_1_out;

  Bit_Extender #(.in_width(16), .out_width(4), .\type ("zero")) bit_extender_1 (
    .in(bitToCheck), .out(bit_extender_1_out));
  Multiplexer #(.select(4)) multiplexer_1 (
    .in0(bits[0]), .in1(bits[1]), .in2(bits[2]), .in3(bits[3]), .in4(bits[4]), .in5(bits[5]), .in6(bits[6]),
    .in7(bits[7]), .in8(bits[8]), .in9(bits[9]), .in10(bits[10]), .in11(bits[11]), .in12(bits[12]),
    .in13(bits[13]), .in14(bits[14]), .in15(bits[15]), .out(\bit ), .sel(bit_extender_1_out));
endmodule

module nibbleIfy (
  input  [15:0] in1,
  input  [15:0] in2,
  output [3:0] out_3,
  output [3:0] out_4,
  output [3:0] out_5,
  output [3:0] out_6,
  output [3:0] out_7,
  output [3:0] out_8,
  output [3:0] out_9,
  output [3:0] out_10
);


  assign out_3 = in1[3:0];
  assign out_4 = in2[3:0];
  assign out_5 = in1[7:4];
  assign out_6 = in2[7:4];
  assign out_7 = in1[11:8];
  assign out_8 = in2[11:8];
  assign out_9 = in1[15:12];
  assign out_10 = in2[15:12];
endmodule

module nibblifySingleInput (
  input  [15:0] in_1,
  output [3:0] out_2,
  output [3:0] out_3,
  output [3:0] out_4,
  output [3:0] out_5
);


  assign out_2 = in_1[3:0];
  assign out_3 = in_1[7:4];
  assign out_4 = in_1[11:8];
  assign out_5 = in_1[15:12];
endmodule

module bitExtendAll1sor0s (
  input  in_1,
  output [15:0] out_2
);

  assign out_2 = {{15{in_1}}, in_1};  // Bit_Extender bit_extender_1
endmodule

module SoundChip (
  input  enable,
  input  [4:0] sel
);

  Decoder #(.select(5)) decoder_1 (
    .sel(sel), .en(enable));  // open: out0, out1, out2, out3, out4, out5, out6, out7, out8, out9, out10, out11, out12, out13, out14, out15, out16, out17, out18, out19, out20, out21, out22, out23, out24, out25, out26, out27, out28, out29, out30, out31
  // Buzzer #(.vol_width(16), .waveform("Square")) buzzer_1: pin names not known
  // Buzzer #(.vol_width(16), .waveform("Square")) buzzer_2: pin names not known
  // Buzzer #(.vol_width(16), .waveform("Square")) buzzer_3: pin names not known
  // Buzzer #(.vol_width(16), .waveform("Square")) buzzer_4: pin names not known
  // Buzzer #(.vol_width(16), .waveform("Triangle")) buzzer_5: pin names not known
  // Buzzer #(.vol_width(16), .waveform("Triangle")) buzzer_6: pin names not known
  // Buzzer #(.vol_width(16), .waveform("Triangle")) buzzer_7: pin names not known
  // Buzzer #(.vol_width(16), .waveform("Triangle")) buzzer_8: pin names not known
  // Buzzer #(.vol_width(16), .waveform("Sawtooth")) buzzer_9: pin names not known
  // Buzzer #(.vol_width(16), .waveform("Sawtooth")) buzzer_10: pin names not known
  // Buzzer #(.vol_width(16), .waveform("Sawtooth")) buzzer_11: pin names not known
  // Buzzer #(.vol_width(16), .waveform("Sawtooth")) buzzer_12: pin names not known
  // Buzzer #(.vol_width(16), .waveform("Noise")) buzzer_13: pin names not known
  // Buzzer #(.vol_width(16), .waveform("Noise")) buzzer_14: pin names not known
  // Buzzer #(.vol_width(16), .waveform("Noise")) buzzer_15: pin names not known
  // Buzzer #(.vol_width(16), .waveform("Noise")) buzzer_16: pin names not known
  // Buzzer #(.vol_width(16)) buzzer_17: pin names not known
  // Buzzer #(.vol_width(16)) buzzer_18: pin names not known
  // Buzzer #(.vol_width(16)) buzzer_19: pin names not known
  // Buzzer #(.vol_width(16)) buzzer_20: pin names not known
endmodule

module sine (
  input  [15:0] in_1
);

  wire [15:0] fpdivider_1_out, fpdivider_2_out, fpdivider_3_out, fpmultiplier_1_out, fpmultiplier_2_out;

  FPMultiplier #(.fpwidth(16)) fpmultiplier_1 (.a(in_1), .b(in_1), .out(fpmultiplier_1_out));
  FPDivider #(.fpwidth(16)) fpdivider_1 (.a(fpmultiplier_1_out), .b(16'h4600), .out(fpdivider_1_out));
  FPDivider #(.fpwidth(16)) fpdivider_2 (.a(fpmultiplier_1_out), .b(16'h4d00), .out(fpdivider_2_out));
  FPDivider #(.fpwidth(16)) fpdivider_3 (.a(fpmultiplier_1_out), .b(16'h5140), .out(fpdivider_3_out));
  FPMultiplier #(.fpwidth(16)) fpmultiplier_2 (.a(fpdivider_2_out), .b(fpdivider_3_out), .out(fpmultiplier_2_out));
  FPMultiplier #(.fpwidth(16)) fpmultiplier_3 (.a(fpdivider_1_out), .b(fpmultiplier_2_out));  // open: out
endmodule

module fp16Tofp32 (
  input  [15:0] FP16
);
endmodule

module ALU32 (
  input  [15:0] in1L,
  input  [15:0] in1H,
  input  [15:0] in2L,
  input  [15:0] in2H
);

  wire [31:0] adder_1_out, divider_1_out, divider_2_out, fpadder_1_out, fpdivider_1_out, fpmultiplier_1_out,
       fpnegator_1_p2, fpsubtractor_1_out, inttofp_1_p2, multiplier_1_out, multiplier_2_out, subtractor_1_out;

  Adder #(.width(32)) adder_1 (.a({in1H, in1L}), .b({in2H, in2L}), .out(adder_1_out));  // open: cin, cout
  Subtractor #(.width(32)) subtractor_1 (
    .a({in1H, in1L}), .b({in2H, in2L}), .out(subtractor_1_out));  // open: bin, bout
  Multiplier #(.width(32)) multiplier_1 (
    .a({in1H, in1L}), .b({in2H, in2L}), .out(multiplier_1_out));  // open: cin, cout
  Multiplier #(.mode("twosComplement"), .width(32)) multiplier_2 (
    .a({in1H, in1L}), .b({in2H, in2L}), .out(multiplier_2_out));  // open: cin, cout
  Divider #(.width(32)) divider_1 (.a({in1H, in1L}), .b({in2H, in2L}), .out(divider_1_out));  // open: upper, rem
  Divider #(.mode("twosComplement"), .width(32)) divider_2 (
    .a({in1H, in1L}), .b({in2H, in2L}), .out(divider_2_out));  // open: upper, rem
  FPAdder fpadder_1 (.a({in1H, in1L}), .b({in2H, in2L}), .out(fpadder_1_out));
  FPSubtractor fpsubtractor_1 (.a({in1H, in1L}), .b({in2H, in2L}), .out(fpsubtractor_1_out));
  FPMultiplier fpmultiplier_1 (.a({in1H, in1L}), .b({in2H, in2L}), .out(fpmultiplier_1_out));
  FPDivider fpdivider_1 (.a({in1H, in1L}), .b({in2H, in2L}), .out(fpdivider_1_out));
  // FPNegator fpnegator_1: pin names not known; wires that end beside it: {in1H, in1L}, fpnegator_1_p2
  // IntToFP #(.width(32)) inttofp_1: pin names not known; wires that end beside it: {in1H, in1L}, inttofp_1_p2
  Multiplexer #(.select(6), .width(32)) multiplexer_1 (
    .in0({in1H, in1L}), .in1(adder_1_out), .in2(subtractor_1_out), .in3(multiplier_1_out),
    .in4(multiplier_2_out), .in5(divider_1_out), .in6(divider_2_out), .in7(fpadder_1_out),
    .in8(fpsubtractor_1_out), .in9(fpmultiplier_1_out), .in10(fpdivider_1_out), .in11(fpnegator_1_p2),
    .in12(inttofp_1_p2));  // open: in13, in14, in15, in16, in17, in18, in19, in20, in21, in22, in23, in24, in25, in26, in27, in28, in29, in30, in31, in32, in33, in34, in35, in36, in37, in38, in39, in40, in41, in42, in43, in44, in45, in46, in47, in48, in49, in50, in51, in52, in53, in54, in55, in56, in57, in58, in59, in60, in61, in62, in63, out, sel
endmodule
